# Fritzing sketch Sketch-Verkabelung Pi-Stepper (saved by Fritzing 0.9.3b)

parts:
  M2 = Stepper Motor - Bipolar
  DRV_1 = DRV 8825 Stepper Motor Carrier, High Current [part_number="DRV 8825"]
  Raspberry_Pi1 = Raspberry Pi 2
  DRV_2 = DRV 8825 Stepper Motor Carrier, High Current [part_number="DRV 8825"]
  M3 = Stepper Motor - Bipolar

nets:
  N1: M2.A, DRV_1.OUT_2B
  N2: M2.C, DRV_1.OUT_2A
  N3: M2.B, DRV_1.OUT_1A
  N4: M2.D, DRV_1.OUT_1B
  3V3: DRV_1.MS1, DRV_1.MS2, Raspberry_Pi1.3v3, Raspberry_Pi1.3V3, DRV_2.MS1, DRV_2.MS2
  N5: DRV_1.STEP, Raspberry_Pi1.GPIO10
  N6: DRV_1.DIRECTION, Raspberry_Pi1.GPIO9
  12V: DRV_1.VOLTAGE_DD, DRV_2.VOLTAGE_DD
  N7: Raspberry_Pi1.GPIO2, DRV_2.STEP
  N8: Raspberry_Pi1.GPIO3, DRV_2.DIRECTION
  N9: DRV_2.OUT_2B, M3.A
  N10: DRV_2.OUT_2A, M3.C
  N11: DRV_2.OUT_1A, M3.B
  N12: DRV_2.OUT_1B, M3.D
